# Fritzing sketch Bonsamatic (saved by Fritzing 0.8.0b)
breadboards: 1

parts:
  U1 = atmega168 [package=dip]
  R1 = Resistor [tolerance=±5% resistance=10k package=THT]
  C1 = Ceramic Capacitor [capacitance=100nF package="100 mil [THT, multilayer]"]
  C2 = Ceramic Capacitor [capacitance=100nF package="100 mil [THT, multilayer]"]
  XTAL1 = Crystal [frequency="16 Mhz" package=THT]
  C3 = Ceramic Capacitor [capacitance=22pF voltage=20V package="100 mil [THT, multilayer]"]
  C4 = Ceramic Capacitor [capacitance=22pF voltage=20V package="100 mil [THT, multilayer]"]
  R2 = Resistor [tolerance=±5% resistance=330 package=THT]
  LED = LED - 5mm [color="Red (633nm)" package="5 mm [THT]"]
  U2 = Voltage Regulator - 5V [package="TO220 [THT]"]
  R3 = Resistor [tolerance=±5% resistance=10k package=THT]
  Display = LED - 5mm [color="Red (633nm)" package="5 mm [THT]"]
  Power_plug1 = Power plug
  C5 = Electrolytic Capacitor [capacitance=10µF voltage=50V package="100 mil [THT, electrolytic]"]
  C6 = Electrolytic Capacitor [capacitance=10µF voltage=50V package="100 mil [THT, electrolytic]"]
  RE1 = Rotary Encoder [package=THT]
  S1 = Toggle Switch [package=THT]
  R4 = Resistor [tolerance=±5% resistance=10k package=THT]
  R5 = Resistor [tolerance=±5% resistance=10k package=THT]
  R6 = Resistor [tolerance=±5% resistance=10k package=THT]
  R7 = Resistor [tolerance=±5% resistance=10k package=THT]
  C7 = Ceramic Capacitor [capacitance=100nF package="100 mil [THT, multilayer]"]
  Q1 = NPN-Transistor [package="TO92 [THT]"]
  M1 = DC Motor
  D1 = Rectifier Diode [part_number=1N4001 package="300 mil [THT]"]
  C8 = Ceramic Capacitor [capacitance=100nF package="100 mil [THT, multilayer]"]
  C9 = Electrolytic Capacitor [capacitance=4.7µF voltage=50V package="100 mil [THT, electrolytic]"]
  J1 = female pin header, 5 pins [form="♀ (female)"]

nets:
  N1: U1.RESET, R1.Pin_1, C7.0
  N2: U1.D0_(RX), J1.pin3
  N3: U1.D1_(TX), J1.pin4
  N4: U1.D2, U1.D3_(PWM), RE1.EncoderPinA, RE1.EncoderPinB, R4.Pin_1, R5.Pin_1
  N5: U1.VCC, U1.AVCC, R1.Pin_0, C1.0, C2.1, U2.output_voltage, C6.+, S1.COM, R5.Pin_0
  GND: U1.GND, C1.1, C2.0, C3.1, C4.1, LED.cathode, U2.GND, Display.cathode, Power_plug1.GND, C6.-, RE1.EncoderPinC, R6.Pin_0, R7.Pin_0, Q1.E, C9.+, J1.pin2
  N6: U1.XLAT1, XTAL1.pin_0, C3.0
  N7: U1.XLAT2, XTAL1.pin_1, C4.0
  N8: U1.D5_(PWM), Q1.B
  N9: U1.D7, S1.L1, R7.Pin_1
  N10: U1.D8, S1.L2, R6.Pin_1
  N11: U1.D9_(PWM), R3.Pin_0
  N12: U1.D13, R2.Pin_0
  N13: R2.Pin_1, LED.anode
  N14: U2.input_voltage, Power_plug1.VCC, C5.+, M1.pin_2, D1.cathode, C8.1, C9.-
  N15: R3.Pin_1, Display.anode
  N16: C7.1, J1.pin5
  N17: Q1.C, M1.pin_1, D1.anode, C8.0

notes:
  analog display
