# Fritzing sketch bonsa (saved by Fritzing 0.9.0b)
breadboards: 1

parts:
  U1 = atmega168 [package=dip]
  R1 = Resistor [tolerance=±5% resistance=10k package=THT]
  C1 = Ceramic Capacitor [capacitance=100nF package="100 mil [THT, multilayer]"]
  C2 = Ceramic Capacitor [capacitance=100nF package="100 mil [THT, multilayer]"]
  Crystal = Crystal [frequency="16 Mhz" package=THT]
  C3 = Ceramic Capacitor [capacitance=22pF voltage=20V package="100 mil [THT, multilayer]"]
  C4 = Ceramic Capacitor [capacitance=22pF voltage=20V package="100 mil [THT, multilayer]"]
  R2 = Resistor [tolerance=±5% resistance=330 package=THT]
  LED = LED - 5mm [color="Red (633nm)" package="5 mm [THT]"]
  U2 = Voltage Regulator - 5V [package="TO220 [THT]"]
  R3 = Resistor [tolerance=±5% resistance=10k package=THT]
  Power_plug_+12V = Power plug
  C5 = Electrolytic Capacitor [capacitance=10µF voltage=50V package="100 mil [THT, electrolytic]"]
  C6 = Electrolytic Capacitor [capacitance=10µF voltage=50V package="100 mil [THT, electrolytic]"]
  Switch = Toggle Switch [package=THT]
  R5 = Resistor [tolerance=±5% resistance=10k package=THT]
  R6 = Resistor [tolerance=±5% resistance=10k package=THT]
  R7 = Resistor [tolerance=±5% resistance=10k package=THT]
  C7 = Ceramic Capacitor [capacitance=100nF package="100 mil [THT, multilayer]"]
  Q1 = NPN-Transistor [package="TO92 [THT]"]
  Pump = DC Motor
  D1 = Rectifier Diode [part_number=1N4001 package="300 mil [THT]"]
  C8 = Ceramic Capacitor [capacitance=100nF package="100 mil [THT, multilayer]"]
  C9 = Electrolytic Capacitor [capacitance=4.7µF voltage=50V package="100 mil [THT, electrolytic]"]
  Header = female pin header, 5 pins [form="♀ (female)"]
  R8 = Resistor [tolerance=±5% resistance=10k package=THT]
  Rotary_Encoder = Rotary Encoder [package=THT]
  meter = Analog meter [package=THT]

nets:
  N1: U1.RESET, R1.Pin_1, C7.0
  N2: U1.D0_(RX), Header.pin3
  N3: U1.D1_(TX), Header.pin4
  N4: U1.D2, R8.Pin_1, Rotary_Encoder.EncoderPinA
  N5: U1.D3_(PWM), R5.Pin_1, Rotary_Encoder.EncoderPinB
  N6: U1.VCC, U1.AVCC, R1.Pin_0, C1.0, C2.1, U2.output_voltage, C6.+, Switch.COM, R5.Pin_0, Header.pin1, R8.Pin_0
  GND: U1.GND, C1.1, C2.0, C3.1, C4.1, LED.cathode, U2.GND, Power_plug_+12V.GND, C5.-, C6.-, R6.Pin_0, R7.Pin_0, Q1.E, C9.-, Header.pin2, Rotary_Encoder.EncoderPinC, meter.pin2
  N7: U1.XLAT1, Crystal.pin_0, C3.0
  N8: U1.XLAT2, Crystal.pin_1, C4.0
  N9: U1.D5_(PWM), Q1.B
  N10: U1.D7, Switch.L1, R7.Pin_1
  N11: U1.D8, Switch.L2, R6.Pin_1
  N12: U1.D9_(PWM), R3.Pin_0
  N13: U1.D13, R2.Pin_0
  N14: R2.Pin_1, LED.anode
  N15: U2.input_voltage, Power_plug_+12V.VCC, C5.+, Pump.pin_2, D1.cathode, C8.1, C9.+
  N16: R3.Pin_1, meter.pin1
  N17: C7.1, Header.pin5
  N18: Q1.C, Pump.pin_1, D1.anode, C8.0

custom parts:
  Rotary Encoder: Rotary Encoder from ALPS STEC12E07.
